# Fritzing sketch updated_wiring_only_breath2 (saved by Fritzing 1.0.6)
breadboards: 2

parts:
  A1 = Teensy 4.0
  Part1 = Adafruit MPR121 [part_number="Adafruit #1982"]
  A2 = MPXV7002DP Module Transducer Differential Pressure Sensor
  Part2 = Thumb Joystick
  R1 = Resistor [tolerance=±10% resistance=10k package="2512 [SMD]"]
  R2 = Resistor [tolerance=±1% resistance=22k package="2512 [SMD]"]
  U1 = LM 358 Dual Op-Amp [package="DIP8 [THT]"]
  C1 = Capacitor [package=cap-pth-large]
  C2 = Capacitor [package=cap-pth-large]
  GY2 = MPU-6050 Board GY-521 [form="♀ (female)" package=THT]
  U2 = LM 358 Dual Op-Amp [package="DIP8 [THT]"]
  C3 = Capacitor [package=cap-pth-large]
  C4 = Capacitor [package=cap-pth-large]
  A3 = Teensy 4.0
  A4 = MPXV7002DP Module Transducer Differential Pressure Sensor
  R3 = Resistor [tolerance=±1% resistance=22k package="2512 [SMD]"]
  R4 = Resistor [tolerance=±10% resistance=10k package="2512 [SMD]"]

nets:
  GND: A1.pin_1, A1.pin_17, A1.pin_32, Part1.GND, A2.GND, Part2.GND, R2.Pin_1, U1.connector3, C1.2, C2.2, GY2.pin2
  N1: A1.pin_4, Part2.SEL
  N2: A1.pin_21, U1.connector0, U1.connector1
  N3: A1.pin_23, Part1.SCL
  N4: A1.pin_24, Part1.SDA
  N5: A1.pin_25, GY2.pin4
  N6: A1.pin_26, GY2.pin3
  N7: A1.pin_27, Part2.HORZ
  N8: A1.pin_28, Part2.VERT
  N9: A1.pin_31, Part1.3.3V, GY2.pin1
  VCC: A1.pin33, A2.VCC, Part2.VCC, U1.connector7, C2.1
  N10: A2.ANLG, R1.Pin_0
  N11: R1.Pin_1, R2.Pin_0, U1.connector2, C1.1
  N12: U2.connector0, U2.connector1, A3.pin_21
  N13: U2.connector2, C4.1, R3.Pin_0, R4.Pin_1
  N14: U2.connector3, C3.2, C4.2, A3.pin_1, A3.pin_32, A4.GND, R3.Pin_1
  N15: U2.connector7, C3.1, A3.pin33, A4.VCC
  N16: A4.ANLG, R4.Pin_0

notes:
  104 (100nF) for power decoupling amp
  104 for signal filter from Vscaled to ground (22nF)

custom parts:
  Teensy 4.0: The Teensy is a complete USB-based microcontoller development system, in a very small footprint, capable of implementing many types of projects. All programming is done via the USB port. No special programmer is needed, only a standard micro-USB cable and a PC or Macintosh with a USB port. (Oct 2023 added the VBUS pad at user request.)
  Adafruit MPR121: Add lots of touch sensors to your next microcontroller project with this easy-to-use 12-channel capacitive touch sensor breakout board, starring the MPR121. This chip can handle up to 12 individual touch pads. The MPR121 has support for only I2C, which can be implemented with nearly any microcontroller. You can select one of 4 addresses with the ADDR pin, for a total of 48 capacitive touch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
  MPXV7002DP Module Transducer Differential Pressure Sensor: The MPXV7002 series piezoresistive transducer in a small footprint package (SOP) is a state-of-the-art monolithic silicon pressure sensor designed for a wide range of applications, particularly those using a microcontroller or microprocessor with A/D inputs. This patented single-element transducer combines advanced microhinging techniques, thin-film metallization, and bipolar processing to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
  MPU-6050 Board GY-521: Acelerometro y Giroscopio MPU-6050 Board GY-521
