# Fritzing sketch wiring (saved by Fritzing 1.0.6)
breadboards: 1

parts:
  A1 = Teensy 4.0
  Part1 = Adafruit MPR121 [part_number="Adafruit #1982"]
  GY1 = MPU-6050 Board GY-521 [form="♀ (female)" package=THT]
  A2 = MPXV7002DP Module Transducer Differential Pressure Sensor
  R1 = Resistor [tolerance=±5% resistance=1k package="2512 [SMD]"]
  R2 = Resistor [tolerance=±5% resistance=2.2k package="2512 [SMD]"]
  Part2 = Thumb Joystick

nets:
  GND: A1.pin_1, A1.pin_17, A1.pin_32, Part1.GND, GY1.pin2, A2.GND, Part2.GND
  N1: A1.pin_4, Part2.SEL
  N2: A1.pin_21, R1.Pin_1, R2.Pin_0
  N3: A1.pin_23, Part1.SCL
  N4: A1.pin_24, Part1.SDA
  N5: A1.pin_25, GY1.pin4
  N6: A1.pin_26, GY1.pin3
  N7: A1.pin_27, Part2.HORZ
  N8: A1.pin_28, Part2.VERT
  N9: A1.pin_31, Part1.3.3V, GY1.pin1, R2.Pin_1
  VCC: A1.pin33, A2.VCC, Part2.VCC
  N10: A2.ANLG, R1.Pin_0

custom parts:
  Teensy 4.0: The Teensy is a complete USB-based microcontoller development system, in a very small footprint, capable of implementing many types of projects. All programming is done via the USB port. No special programmer is needed, only a standard micro-USB cable and a PC or Macintosh with a USB port. (Oct 2023 added the VBUS pad at user request.)
  Adafruit MPR121: Add lots of touch sensors to your next microcontroller project with this easy-to-use 12-channel capacitive touch sensor breakout board, starring the MPR121. This chip can handle up to 12 individual touch pads. The MPR121 has support for only I2C, which can be implemented with nearly any microcontroller. You can select one of 4 addresses with the ADDR pin, for a total of 48 capacitive touch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
  MPU-6050 Board GY-521: Acelerometro y Giroscopio MPU-6050 Board GY-521
  MPXV7002DP Module Transducer Differential Pressure Sensor: The MPXV7002 series piezoresistive transducer in a small footprint package (SOP) is a state-of-the-art monolithic silicon pressure sensor designed for a wide range of applications, particularly those using a microcontroller or microprocessor with A/D inputs. This patented single-element transducer combines advanced microhinging techniques, thin-film metallization, and bipolar processing to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
