# Fritzing sketch wiring (saved by Fritzing 1.0.6)
breadboards: 1

parts:
  A1 = Teensy 4.0
  A2 = MPXV7002DP Module Transducer Differential Pressure Sensor
  Part2 = Thumb Joystick
  R1 = Resistor [tolerance=±10% resistance=10k package="2512 [SMD]"]
  R2 = Resistor [tolerance=±1% resistance=22k package="2512 [SMD]"]
  U1 = LM 358 Dual Op-Amp [package="DIP8 [THT]"]
  C1 = Capacitor [package=cap-pth-large]
  C2 = Capacitor [package=cap-pth-large]
  GY2 = MPU-6050 Board GY-521 [form="♀ (female)" package=THT]
  Part3 = Adafruit CAP1188 - 8-Key Capacitive Touch Sensor Breakout [part_number="Adafruit #1602"]

nets:
  GND: A1.pin_1, A1.pin_17, A1.pin_32, A2.GND, Part2.GND, R2.Pin_1, U1.connector3, C1.2, C2.2, GY2.pin2, Part3.GND
  N1: A1.pin_4, Part2.SEL
  N2: A1.pin_7, Part3.RESET
  N3: A1.pin_16, A1.pin_31, GY2.pin1, Part3.VIN
  N4: A1.pin_21, U1.connector0, U1.connector1
  N5: A1.pin_23, Part3.SCK
  N6: A1.pin_24, Part3.SDA/MISO
  N7: A1.pin_25, GY2.pin4
  N8: A1.pin_26, GY2.pin3
  N9: A1.pin_27, Part2.HORZ
  N10: A1.pin_28, Part2.VERT
  VCC: A1.pin33, A2.VCC, Part2.VCC, U1.connector7, C2.1
  N11: A2.ANLG, R1.Pin_0
  N12: R1.Pin_1, R2.Pin_0, U1.connector2, C1.1

notes:
  104 (100nF) for power decoupling amp
  104 for signal filter from Vscaled to ground (22nF)

custom parts:
  Teensy 4.0: The Teensy is a complete USB-based microcontoller development system, in a very small footprint, capable of implementing many types of projects. All programming is done via the USB port. No special programmer is needed, only a standard micro-USB cable and a PC or Macintosh with a USB port. (Oct 2023 added the VBUS pad at user request.)
  MPXV7002DP Module Transducer Differential Pressure Sensor: The MPXV7002 series piezoresistive transducer in a small footprint package (SOP) is a state-of-the-art monolithic silicon pressure sensor designed for a wide range of applications, particularly those using a microcontroller or microprocessor with A/D inputs. This patented single-element transducer combines advanced microhinging techniques, thin-film metallization, and bipolar processing to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
  MPU-6050 Board GY-521: Acelerometro y Giroscopio MPU-6050 Board GY-521
  Adafruit CAP1188 - 8-Key Capacitive Touch Sensor Breakout: Add lots of touch sensors to your next microcontroller project with this easy-to-use 8-channel capacitive touch sensor breakout board, starring the CAP1188. This chip can handle up to 8 individual touch pads, and has a very nice feature that makes it stand out for us: it will light up the 8 onboard LEDs when the matching touch sensor fires to help you debug your sensor setup. The CAP1188 has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
